# Fritzing sketch Pengukur_Suhu_Ruangan (saved by Fritzing 0.9.3b)
breadboards: 1

parts:
  Part2 = LCD1602-I2C
  WeMos_D1_Mini1 = WeMos D1 Mini  # not connected
  LED7 = smd LED [color="Red (633nm)" package="1206 [SMD]"]  # not connected
  LED8 = smd LED [color="Yellow (595nm)" package="1206 [SMD]"]  # not connected
  LED9 = smd LED [color="Green (555nm)" package="1206 [SMD]"]  # not connected
  R7 = Resistor [tolerance=±5% resistance=220 package="2010 [SMD]"]  # not connected
  R8 = Resistor [tolerance=±5% resistance=220 package="2010 [SMD]"]  # not connected
  R9 = Resistor [tolerance=±5% resistance=220 package="2010 [SMD]"]  # not connected
  JP3 = Header 8 [package=1x08_smd_alt]  # not connected
  JP4 = Header 8 [package=1x08_smd_alt]
  DHT1 = DHT11 Humitidy and Temperature Sensor

nets:
  GND: Part2.GND, JP4.2, DHT1.GND
  VCC: Part2.VCC, JP4.1, DHT1.VDD
  N1: Part2.SDA, JP4.5
  N2: Part2.SCL, JP4.6
  N3: JP4.3, DHT1.DATA

custom parts:
  LCD1602-I2C: A standard character display, usually with 2x16 characters. Comes in many colors with LCM1602 IIC attached.
  DHT11 Humitidy and Temperature Sensor: DHT11 Humidity and Temperature Sensor
